# Fritzing sketch SmartPoolFritz (saved by Fritzing 0.9.9b)
breadboards: 3

parts:
  Breadboard4 = Breadboard Split Power
  Breadboard5 = Breadboard Split Power
  Teensy_3_3 = Teensy 3.1
  WIZ820io1 = WIZ820io [part_number=WIZ820io]
  Part3 = 12 NeoPixel Ring [part_number=1643]
  S1 = Pushbutton [package="[THT]"]
  R1 = Resistor [tolerance=±5% resistance=220 package="2512 [SMD]"]
  LED1 = smd LED [color="White (4500K)" package="1206 [SMD]"]
  R2 = PHOTOCELL [package=photocell]
  R3 = Resistor [tolerance=±5% resistance=10000 package="2512 [SMD]"]
  J1 = Basic Servo
  Part4 = Adafruit TCS34725 RGB Color Sensor [part_number="Adafruit #1334"]
  OLED_I2C1 = OLED 128x64 I2C Monochrome Display

nets:
  3V3: Breadboard4.pin3Y, Breadboard4.pin15Y, Breadboard4.pin17Y, Breadboard4.pin21Y, Breadboard4.pin29Y, Breadboard5.pin3Y, Breadboard5.pin15Y, Breadboard5.pin17Y, Breadboard5.pin29Y, Teensy_3_3.3V3, Part3.VDD, R1.Pin_1, R2.P$1, J1.vcc, Part4.VIN
  GND: Breadboard4.pin4Z, Breadboard4.pin20Z, Breadboard4.pin29Z, Breadboard5.pin3Z, Breadboard5.pin11Z, Breadboard5.pin28Z, Teensy_3_3.D10, WIZ820io1.GND, WIZ820io1.SCLK, Part3.GND, S1.Pin_3, S1.Pin_4, LED1.cathode, R3.Pin_1, J1.gnd, Part4.GND, OLED_I2C1.GND
  N1: Teensy_3_3.D9, WIZ820io1.nRESET
  N2: Teensy_3_3.D12, WIZ820io1.MISO
  VIN: Teensy_3_3.Vin, WIZ820io1.VIN
  N3: WIZ820io1.MOSI, OLED_I2C1.VDD
  N4: S1.Pin_1, S1.Pin_2
  N5: R2.P$2, R3.Pin_0
  N6: Part4.+3V3, Part4.SCL, OLED_I2C1.SDA
  N7: Part4.SDA, Part4.INT, OLED_I2C1.SCK

custom parts:
  Breadboard Split Power: A custom 6 pin per group power supply strip where the top row (ground) is all bussed together and the bottom row (+V) is split in two groups of 12 pins. This version is modified to be a loadable part and was rescaled to be on the standard 1px = 1thou grid with the size set in inches
  12 NeoPixel Ring: 12 ultra bright smart LED NeoPixels are arranged in a circle with 1.5" (37mm) outer diameter. The rings are 'chainable' - connect the output pin of one to the input pin of another. Use only one microcontroller pin to control as many as you can chain together! Each LED is addressable as the driver chip is inside the LED. Each one has ~18mA constant current drive so the color will be very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
  Pushbutton: A generic pushbutton.
  Adafruit TCS34725 RGB Color Sensor: Your electronics can now see in dazzling color with this lovely color light sensor. We found the best color sensor on the market, the TCS34725, which has RGB and Clear light sensing elements. An IR blocking filter, integrated on-chip and localized to the color sensing photodiodes, minimizes the IR spectral component of the incoming light and allows color measurements to be made accurately. The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
